// Logisim project 5_.circ as structural Verilog: 1 circuit, main circuit main
module main (
  input  in_1,
  input  in_2,
  input  in_3,
  input  in_4,
  output out_5,
  output out_6,
  output out_7,
  output out_8
);

  wire nor_1_out, nor_4_out, nor_5_out;

  nor nor_1 (nor_1_out, in_2, in_2);
  nor nor_2 (out_7, in_3, out_8);
  nor nor_3 (out_8, out_7, in_4);
  nor nor_4 (nor_4_out, nor_1_out, in_1);
  nor nor_5 (nor_5_out, in_1, in_2);
  nor nor_6 (out_5, nor_4_out, out_6);
  nor nor_7 (out_6, out_5, nor_5_out);

  // Notes on the sheet:
  //   D Latch
  //   D Flip Flop
endmodule
