// Logisim project 6_.circ as structural Verilog: 1 circuit, main circuit main
module main (
  input  [2:0] in_1,
  input  [2:0] Address,
  input  Write,
  output [2:0] out_4
);

  wire and_1_out, and_2_out, and_3_out, and_4_out, and_5_out, d_ff_1_q, d_ff_2_q, d_ff_3_q, d_ff_5_q,
       d_ff_6_q, d_ff_7_q, d_ff_8_q, d_ff_9_q, d_ff_10_q, d_ff_11_q, d_ff_12_q, d_ff_13_q, d_ff_14_q,
       d_ff_15_q, decoder_1_out2, decoder_1_out3, decoder_1_out4, decoder_1_out5, decoder_1_out6,
       multiplexer_2_out, multiplexer_3_out;

  Decoder #(.select(3)) decoder_1 (
    .out2(decoder_1_out2), .out3(decoder_1_out3), .out4(decoder_1_out4), .out5(decoder_1_out5),
    .out6(decoder_1_out6), .sel(Address));  // open: out0, out1, out7, en
  and and_1 (and_1_out, decoder_1_out2, Write);
  and and_2 (and_2_out, decoder_1_out4, Write);
  and and_3 (and_3_out, decoder_1_out5, Write);
  and and_4 (and_4_out, decoder_1_out6, Write);
  and and_5 (and_5_out, decoder_1_out3, Write);
  D_Flip_Flop d_ff_1 (.D(in_1[2]), .clk(and_1_out), .Q(d_ff_1_q), .reset(decoder_1_out2));  // open: Qn, preset
  D_Flip_Flop d_ff_2 (.D(in_1[2]), .clk(and_5_out), .Q(d_ff_2_q), .reset(decoder_1_out3));  // open: Qn, preset
  D_Flip_Flop d_ff_3 (.D(in_1[2]), .clk(decoder_1_out4), .Q(d_ff_3_q), .reset(and_2_out));  // open: Qn, preset
  D_Flip_Flop d_ff_4 (.D(in_1[2]), .clk(and_3_out), .Q(decoder_1_out4), .reset(decoder_1_out5));  // open: Qn, preset
  D_Flip_Flop d_ff_5 (.D(in_1[2]), .clk(and_4_out), .Q(d_ff_5_q), .reset(decoder_1_out6));  // open: Qn, preset
  D_Flip_Flop d_ff_6 (.D(in_1[1]), .clk(and_1_out), .Q(d_ff_6_q), .reset(decoder_1_out2));  // open: Qn, preset
  D_Flip_Flop d_ff_7 (.D(in_1[1]), .clk(and_5_out), .Q(d_ff_7_q), .reset(decoder_1_out3));  // open: Qn, preset
  D_Flip_Flop d_ff_8 (.D(in_1[1]), .clk(decoder_1_out4), .Q(d_ff_8_q), .reset(and_2_out));  // open: Qn, preset
  D_Flip_Flop d_ff_9 (.D(in_1[1]), .clk(and_3_out), .Q(d_ff_9_q), .reset(decoder_1_out5));  // open: Qn, preset
  D_Flip_Flop d_ff_10 (.D(in_1[1]), .clk(and_4_out), .Q(d_ff_10_q), .reset(decoder_1_out6));  // open: Qn, preset
  D_Flip_Flop d_ff_11 (.D(in_1[0]), .clk(and_1_out), .Q(d_ff_11_q), .reset(decoder_1_out2));  // open: Qn, preset
  D_Flip_Flop d_ff_12 (.D(in_1[0]), .clk(and_5_out), .Q(d_ff_12_q), .reset(decoder_1_out3));  // open: Qn, preset
  D_Flip_Flop d_ff_13 (.D(in_1[0]), .clk(decoder_1_out4), .Q(d_ff_13_q), .reset(and_2_out));  // open: Qn, preset
  D_Flip_Flop d_ff_14 (.D(in_1[0]), .clk(and_3_out), .Q(d_ff_14_q), .reset(decoder_1_out5));  // open: Qn, preset
  D_Flip_Flop d_ff_15 (.D(in_1[0]), .clk(and_4_out), .Q(d_ff_15_q), .reset(decoder_1_out6));  // open: Qn, preset
  Multiplexer multiplexer_1 (.in0(d_ff_2_q), .in1(d_ff_7_q), .sel(d_ff_12_q));  // open: out
  Multiplexer #(.select(2)) multiplexer_2 (
    .in1(d_ff_1_q), .in2(d_ff_6_q), .in3(d_ff_11_q), .out(multiplexer_2_out));  // open: in0, sel
  Multiplexer multiplexer_3 (.in0(d_ff_3_q), .in1(d_ff_8_q), .out(multiplexer_3_out), .sel(d_ff_13_q));
  // Multiplexer multiplexer_4: pin names not known; wires that end beside it: decoder_1_out4, d_ff_9_q, d_ff_14_q
  // Multiplexer multiplexer_5: pin names not known; wires that end beside it: d_ff_5_q, d_ff_10_q, d_ff_15_q
  Multiplexer #(.width(3)) multiplexer_6 (.out(out_4));  // open: in0, in1, sel
endmodule
